// Logisim project Memoria Ram e Rom.circ as structural Verilog: 2 circuits, main circuit main
module main (
  input  NIBBLE_HIGH,
  input  in_2,
  input  in_3,
  input  in_4,
  input  in_5,
  input  in_6,
  input  in_7,
  input  in_8,
  input  in_9,
  input  Endereco,
  input  in_11,
  input  LSB,
  input  in_13,
  input  Clock,
  input  Escrita__0__e_Leitura__1,
  input  in_16,
  output [7:0] Leitor_de_dados,
  output [7:0] out_18
);

  wire Clear_out;

  assign Leitor_de_dados = in_13 ? out_18 : 8'bz;  // Controlled_Buffer controlled_buffer_1
  assign out_18 = in_16 ? Leitor_de_dados : 8'bz;  // Controlled_Buffer controlled_buffer_2
  assign Leitor_de_dados = in_9 ? {NIBBLE_HIGH, in_2, in_3, in_4, in_5, in_6, in_7, in_8} : 8'bz;  // Controlled_Buffer controlled_buffer_3
  Button Clear (.out(Clear_out));
  RAM #(.addrWidth(3)) ram_1 (
    .addr({Endereco, in_11, LSB}), .data(out_18), .sel(1'b1), .clk(Clock), .ld(Escrita__0__e_Leitura__1),
    .clr(Clear_out));

  // Notes on the sheet:
  //   Memoria RAM
  //   Barramento de dados
  //   Fonte
  //   NIBBLE LOW
endmodule

module ROM (
  input  in_1,
  input  in_2,
  input  LSB,
  input  in_4
);

  wire [7:0] rom_1_data;

  ROM_part #(.addrWidth(3)) rom_1 (.addr({in_1, in_2, LSB}), .data(rom_1_data), .sel(in_4));
  Hex_Digit_Display hex_digit_display_1 (.value(rom_1_data[7:4]));  // open: dp
  Hex_Digit_Display hex_digit_display_2 (.value(rom_1_data[3:0]));  // open: dp

  // Notes on the sheet:
  //   Barramento de Endereco
  //   8D ROM
  //   contents of rom_1 (hex, n*v repeats v):
  //   10 3 0 5 16 90 50 22
endmodule
