// Logisim project Roteiro4.circ as structural Verilog
module main (
  input  in_1,
  input  in_2,
  input  in_3,
  input  in_4,
  input  in_5,
  input  in_6,
  input  [2:0] in_7,
  input  in_8,
  input  in_9,
  input  in_10,
  input  in_11,
  input  [2:0] in_12,
  output out_13,
  output out_14
);

  wire controlled_buffer_1_out, controlled_buffer_2_out, controlled_buffer_3_out, controlled_buffer_4_out,
       controlled_buffer_5_out, controlled_buffer_6_out, controlled_buffer_7_out, controlled_buffer_8_out,
       demultiplexer_1_out0, demultiplexer_1_out1, demultiplexer_1_out2, demultiplexer_1_out3,
       demultiplexer_1_out4, demultiplexer_1_out5, demultiplexer_1_out6, demultiplexer_1_out7,
       demultiplexer_2_out0, demultiplexer_2_out1, demultiplexer_2_out2, demultiplexer_2_out3,
       demultiplexer_2_out4, demultiplexer_2_out5, demultiplexer_2_out6, demultiplexer_2_out7, not_1_out,
       not_2_out, not_3_out;

  Demultiplexer #(.select(3)) demultiplexer_1 (
    .out0(demultiplexer_1_out0), .out1(demultiplexer_1_out1), .out2(demultiplexer_1_out2),
    .out3(demultiplexer_1_out3), .out4(demultiplexer_1_out4), .out5(demultiplexer_1_out5),
    .out6(demultiplexer_1_out6), .out7(demultiplexer_1_out7), .in(in_11), .sel(in_12));  // open: en
  Demultiplexer #(.select(3)) demultiplexer_2 (
    .out0(demultiplexer_2_out0), .out1(demultiplexer_2_out1), .out2(demultiplexer_2_out2),
    .out3(demultiplexer_2_out3), .out4(demultiplexer_2_out4), .out5(demultiplexer_2_out5),
    .out6(demultiplexer_2_out6), .out7(demultiplexer_2_out7), .in(in_5), .sel(in_7));  // open: en
  not not_1 (not_1_out, demultiplexer_1_out0);
  not not_2 (not_2_out, demultiplexer_1_out2);
  not not_3 (not_3_out, demultiplexer_1_out7);
  Multiplexer #(.select(3)) multiplexer_1 (
    .in0(not_1_out), .in1(demultiplexer_1_out1), .in2(not_2_out), .in3(demultiplexer_1_out3),
    .in4(demultiplexer_1_out4), .in5(demultiplexer_1_out5), .in6(demultiplexer_1_out6), .in7(not_3_out),
    .out(out_14), .sel(in_12));  // open: en
  assign controlled_buffer_1_out = in_1 ? demultiplexer_2_out0 : 1'bz;  // Controlled_Buffer controlled_buffer_1
  assign controlled_buffer_2_out = in_2 ? demultiplexer_2_out1 : 1'bz;  // Controlled_Buffer controlled_buffer_2
  assign controlled_buffer_3_out = in_3 ? demultiplexer_2_out2 : 1'bz;  // Controlled_Buffer controlled_buffer_3
  assign controlled_buffer_4_out = in_4 ? demultiplexer_2_out3 : 1'bz;  // Controlled_Buffer controlled_buffer_4
  assign controlled_buffer_5_out = in_6 ? demultiplexer_2_out4 : 1'bz;  // Controlled_Buffer controlled_buffer_5
  assign controlled_buffer_6_out = in_8 ? demultiplexer_2_out5 : 1'bz;  // Controlled_Buffer controlled_buffer_6
  assign controlled_buffer_7_out = in_9 ? demultiplexer_2_out6 : 1'bz;  // Controlled_Buffer controlled_buffer_7
  assign controlled_buffer_8_out = in_10 ? demultiplexer_2_out7 : 1'bz;  // Controlled_Buffer controlled_buffer_8
  or or_1 (out_13, controlled_buffer_1_out, controlled_buffer_2_out, controlled_buffer_3_out, controlled_buffer_4_out, controlled_buffer_5_out, controlled_buffer_6_out, controlled_buffer_7_out, controlled_buffer_8_out);
endmodule

module b (
  input  in_1,
  input  in_2,
  input  in_3,
  input  in_4,
  input  in_5,
  input  in_6,
  input  [1:0] A1_A2,
  input  [1:0] B1_B2,
  input  in_9,
  input  in_10,
  input  in_11,
  input  in_12,
  input  in_13,
  input  in_14,
  input  in_15,
  input  in_16,
  input  [1:0] A3_A4,
  input  [1:0] B3_B4,
  input  in_19,
  input  in_20,
  output out_21
);

  wire and_1_out, and_2_out, and_3_out, and_4_out, and_5_out, and_6_out, and_7_out, and_8_out,
       controlled_buffer_1_out, controlled_buffer_2_out, controlled_buffer_3_out, controlled_buffer_4_out,
       controlled_buffer_5_out, controlled_buffer_6_out, controlled_buffer_7_out, controlled_buffer_8_out,
       controlled_buffer_9_out, controlled_buffer_10_out, controlled_buffer_11_out, controlled_buffer_12_out,
       controlled_buffer_13_out, controlled_buffer_14_out, controlled_buffer_15_out,
       controlled_buffer_16_out, demultiplexer_1_out0, demultiplexer_1_out1, demultiplexer_1_out2,
       demultiplexer_1_out3, demultiplexer_2_out0, demultiplexer_2_out1, demultiplexer_2_out2,
       demultiplexer_2_out3, demultiplexer_3_out0, demultiplexer_3_out1, demultiplexer_3_out2,
       demultiplexer_3_out3, demultiplexer_4_out0, demultiplexer_4_out1, demultiplexer_4_out2,
       demultiplexer_4_out3, not_1_out, not_2_out, not_3_out, not_4_out, or_1_out, or_2_out, or_3_out,
       or_4_out, or_5_out, or_6_out, or_7_out, or_8_out, or_9_out;

  Demultiplexer #(.select(2)) demultiplexer_1 (
    .out0(demultiplexer_1_out0), .out1(demultiplexer_1_out1), .out2(demultiplexer_1_out2),
    .out3(demultiplexer_1_out3), .in(1'b1), .sel(A1_A2));  // open: en
  Demultiplexer #(.select(2)) demultiplexer_2 (
    .out0(demultiplexer_2_out0), .out1(demultiplexer_2_out1), .out2(demultiplexer_2_out2),
    .out3(demultiplexer_2_out3), .in(1'b1), .sel(A3_A4));  // open: en
  assign controlled_buffer_1_out = in_1 ? demultiplexer_1_out0 : 1'bz;  // Controlled_Buffer controlled_buffer_1
  assign controlled_buffer_2_out = in_3 ? demultiplexer_1_out1 : 1'bz;  // Controlled_Buffer controlled_buffer_2
  assign controlled_buffer_3_out = in_5 ? demultiplexer_1_out2 : 1'bz;  // Controlled_Buffer controlled_buffer_3
  assign controlled_buffer_4_out = in_9 ? demultiplexer_1_out3 : 1'bz;  // Controlled_Buffer controlled_buffer_4
  assign controlled_buffer_5_out = in_11 ? demultiplexer_2_out0 : 1'bz;  // Controlled_Buffer controlled_buffer_5
  assign controlled_buffer_6_out = in_13 ? demultiplexer_2_out1 : 1'bz;  // Controlled_Buffer controlled_buffer_6
  assign controlled_buffer_7_out = in_15 ? demultiplexer_2_out2 : 1'bz;  // Controlled_Buffer controlled_buffer_7
  assign controlled_buffer_8_out = in_19 ? demultiplexer_2_out3 : 1'bz;  // Controlled_Buffer controlled_buffer_8
  or or_1 (or_1_out, controlled_buffer_1_out, controlled_buffer_2_out, controlled_buffer_3_out, controlled_buffer_4_out);
  or or_2 (or_2_out, controlled_buffer_5_out, controlled_buffer_6_out, controlled_buffer_7_out, controlled_buffer_8_out);
  and and_1 (and_1_out, or_1_out, or_3_out);
  or or_3 (or_3_out, and_2_out, and_3_out);
  and and_2 (and_2_out, or_2_out, 1'b1);
  or or_4 (or_4_out, and_1_out, and_4_out);
  not not_1 (not_1_out, or_1_out);
  and and_3 (and_3_out, not_2_out, 1'b0);
  not not_2 (not_2_out, or_2_out);
  and and_4 (and_4_out, not_1_out, 1'b0);
  or or_5 (or_5_out, 1'b0, or_4_out);
  Demultiplexer #(.select(2)) demultiplexer_3 (
    .out0(demultiplexer_3_out0), .out1(demultiplexer_3_out1), .out2(demultiplexer_3_out2),
    .out3(demultiplexer_3_out3), .in(1'b1), .sel(B1_B2));  // open: en
  Demultiplexer #(.select(2)) demultiplexer_4 (
    .out0(demultiplexer_4_out0), .out1(demultiplexer_4_out1), .out2(demultiplexer_4_out2),
    .out3(demultiplexer_4_out3), .in(1'b1), .sel(B3_B4));  // open: en
  assign controlled_buffer_9_out = in_2 ? demultiplexer_3_out0 : 1'bz;  // Controlled_Buffer controlled_buffer_9
  assign controlled_buffer_10_out = in_4 ? demultiplexer_3_out1 : 1'bz;  // Controlled_Buffer controlled_buffer_10
  assign controlled_buffer_11_out = in_6 ? demultiplexer_3_out2 : 1'bz;  // Controlled_Buffer controlled_buffer_11
  assign controlled_buffer_12_out = in_10 ? demultiplexer_3_out3 : 1'bz;  // Controlled_Buffer controlled_buffer_12
  assign controlled_buffer_13_out = in_12 ? demultiplexer_4_out0 : 1'bz;  // Controlled_Buffer controlled_buffer_13
  assign controlled_buffer_14_out = in_14 ? demultiplexer_4_out1 : 1'bz;  // Controlled_Buffer controlled_buffer_14
  assign controlled_buffer_15_out = in_16 ? demultiplexer_4_out2 : 1'bz;  // Controlled_Buffer controlled_buffer_15
  assign controlled_buffer_16_out = in_20 ? demultiplexer_4_out3 : 1'bz;  // Controlled_Buffer controlled_buffer_16
  or or_6 (or_6_out, controlled_buffer_9_out, controlled_buffer_10_out, controlled_buffer_11_out, controlled_buffer_12_out);
  or or_7 (or_7_out, controlled_buffer_13_out, controlled_buffer_14_out, controlled_buffer_15_out, controlled_buffer_16_out);
  and and_5 (and_5_out, or_6_out, or_8_out);
  or or_8 (or_8_out, and_6_out, and_7_out);
  and and_6 (and_6_out, or_7_out, 1'b1);
  or or_9 (or_9_out, and_5_out, and_8_out);
  not not_3 (not_3_out, or_6_out);
  and and_7 (and_7_out, not_4_out, 1'b0);
  not not_4 (not_4_out, or_7_out);
  and and_8 (and_8_out, not_3_out, 1'b0);
  and and_9 (out_21, or_5_out, or_9_out);
endmodule
